// Logisim project hw4.circ as structural Verilog: 8 circuits, main circuit main
module main (
  input  reset
);

  wire ALU_imme, ALUsrc, and_1_out, and_3_out, beq, blt, Branch, clk, decoder_1_out2, decoder_1_out3,
       decoder_1_out4, decoder_1_out5, decoder_1_out6, decoder_1_out7, decoder_1_out8, decoder_1_out9,
       decoder_1_out10, decoder_1_out11, decoder_1_out13, in_enable, kb_enable, memory_latch_1_oe_latched,
       memory_latch_1_we_latched, MemToReg, Rwe, shift_sig, tty_enable;
  wire [2:0] write_reg;
  wire [3:0] opcode;
  wire [5:0] imme;
  wire [6:0] bit_extender_1_out, kb_out;
  wire [7:7] not_1_out;
  wire [11:6] L;
  wire [14:0] adder_2_out_4;
  wire [15:0] adder_3_out_4, adder_5_out_4, ALU_out, and_2_out, beq_branch, bit_extender_2_out,
       bit_extender_3_out, bit_extender_4_out, bit_extender_5_out, bit_extender_6_out, bit_extender_7_out,
       blt_branch, j_addr, mem_out, memory_latch_1_address_latched, memory_latch_1_data_in_latched,
       multiplexer_2_out, multiplexer_3_out, multiplexer_5_out, multiplexer_6_out, new_pc, pc, pc_1, rs_data,
       rt_data, write_data;

  Clock u_clk (.out(clk));
  SingleReg u_PC (.clock(clk), .enable(1'b1), .in_16bit(new_pc), .reset(reset), .out_16bit(pc));
  Decoder #(.select(4)) decoder_1 (
    .out0(MemToReg), .out1(ALUsrc), .out2(decoder_1_out2), .out3(decoder_1_out3), .out4(decoder_1_out4),
    .out5(decoder_1_out5), .out6(decoder_1_out6), .out7(decoder_1_out7), .out8(decoder_1_out8),
    .out9(decoder_1_out9), .out10(decoder_1_out10), .out11(decoder_1_out11), .out13(decoder_1_out13),
    .out14(tty_enable), .out15(in_enable), .sel(opcode));  // open: out12, en
  adder adder_1 (.a(pc), .b(16'h1), .sub(1'b0), .out_4(pc_1));  // open: overflow
  ROM #(.addrWidth(16), .dataWidth(16)) rom_1 (.addr(pc), .data({opcode, L, imme}));
  or u_Rwe (Rwe, MemToReg, decoder_1_out4, decoder_1_out5, decoder_1_out6, decoder_1_out7, decoder_1_out8, decoder_1_out9, decoder_1_out10, decoder_1_out11, decoder_1_out13, in_enable);
  Keyboard keyboard_1 (.clk(clk), .re(in_enable), .clr(reset), .avail(kb_enable), .data(kb_out));
  or or_1 (Branch, decoder_1_out2, decoder_1_out3);
  or or_2 (ALU_imme, decoder_1_out6, MemToReg, decoder_1_out9);
  Multiplexer #(.select(4), .width(3), .enable("false")) multiplexer_1 (
    .in0(L[8:6]), .in4(imme[5:3]), .in5(imme[5:3]), .in6(L[8:6]), .in7(imme[5:3]), .in8(imme[5:3]),
    .in9(L[8:6]), .in10(imme[5:3]), .in11(imme[5:3]), .in13(3'b111), .in15(imme[5:3]), .out(write_reg),
    .sel(opcode));  // open: in1, in2, in3, in12, in14
  or or_3 (shift_sig, decoder_1_out10, decoder_1_out11);
  Bit_Extender #(.in_width(16), .out_width(7), .\type ("zero")) bit_extender_1 (.in(rs_data), .out(bit_extender_1_out));
  RegisterFile registerfile_1 (
    .read_reg_1(L[11:9]), .read_reg_2(L[8:6]), .write_data(write_data), .reset(reset), .write_reg(write_reg),
    .clock(clk), .r1(rs_data), .r2(rt_data), .write_enable(Rwe));
  TTY #(.rows(13), .cols(80), .trigger("falling")) tty_1 (
    .data(bit_extender_1_out), .clk(clk), .we(tty_enable), .clr(reset));
  assign bit_extender_2_out = {{10{imme[5]}}, imme};  // Bit_Extender bit_extender_2
  assign bit_extender_3_out = {{10{imme[5]}}, imme};  // Bit_Extender bit_extender_3
  assign bit_extender_4_out = {{13{1'b0}}, imme[2:0]};  // Bit_Extender bit_extender_4
  Multiplexer #(.width(16), .enable("false")) multiplexer_2 (
    .in0(ALU_out), .in1(mem_out), .out(multiplexer_2_out), .sel(MemToReg));
  not not_1 (not_1_out[7], kb_enable);
  Multiplexer #(.width(16), .enable("false")) multiplexer_3 (
    .in0(rt_data), .in1(bit_extender_2_out), .out(multiplexer_3_out), .sel(ALUsrc));
  Multiplexer #(.select(4), .width(16), .enable("false")) multiplexer_4 (
    .in0(multiplexer_2_out), .in4(ALU_out), .in5(ALU_out), .in6(ALU_out), .in7(ALU_out), .in8(ALU_out),
    .in9(ALU_out), .in10(ALU_out), .in11(ALU_out), .in13(pc_1), .in15({{8{1'b0}}, not_1_out[7], kb_out}),
    .out(write_data), .sel(opcode));  // open: in1, in2, in3, in12, in14
  Multiplexer #(.width(16), .enable("false")) multiplexer_5 (
    .in0(multiplexer_3_out), .in1(bit_extender_3_out), .out(multiplexer_5_out), .sel(ALU_imme));
  adder adder_2 (.a(rs_data), .b(rt_data), .sub(1'b1), .out_4({blt, adder_2_out_4}));  // open: overflow
  Multiplexer #(.width(16), .enable("false")) multiplexer_6 (
    .in0(multiplexer_5_out), .in1(bit_extender_4_out), .out(multiplexer_6_out), .sel(shift_sig));
  assign bit_extender_5_out = {{10{imme[5]}}, imme};  // Bit_Extender bit_extender_5
  ALU alu_1 (.A(rs_data), .B(multiplexer_6_out), .opcode(opcode), .data_output(ALU_out));
  adder adder_3 (.a(pc_1), .b(bit_extender_5_out), .sub(1'b0), .out_4(adder_3_out_4));  // open: overflow
  and and_1 (and_1_out, Branch, beq);
  assign and_2_out = pc & 16'hf000;  // AND_Gate and_2, 16 bits wide
  assign bit_extender_6_out = {{4{1'b0}}, {L, imme}};  // Bit_Extender bit_extender_6
  nor nor_1 (beq, adder_2_out_4[0], adder_2_out_4[1], adder_2_out_4[2], adder_2_out_4[3], adder_2_out_4[4], adder_2_out_4[5], adder_2_out_4[6], adder_2_out_4[7], adder_2_out_4[9], adder_2_out_4[10], adder_2_out_4[11], adder_2_out_4[12], adder_2_out_4[13], adder_2_out_4[14], blt, adder_2_out_4[8]);
  Multiplexer #(.width(16), .enable("false")) multiplexer_7 (
    .in0(pc_1), .in1(adder_3_out_4), .out(beq_branch), .sel(and_1_out));
  adder adder_4 (.a(and_2_out), .b(bit_extender_6_out), .sub(1'b0), .out_4(j_addr));  // open: overflow
  memory_latch memory_latch_1 (
    .address(ALU_out), .WE(ALUsrc), .clk(clk), .data_in(rt_data),
    .address_latched(memory_latch_1_address_latched), .WE_latched(memory_latch_1_we_latched),
    .OE_latched(memory_latch_1_oe_latched), .data_in_latched(memory_latch_1_data_in_latched));
  Multiplexer #(.select(4), .width(16), .enable("false")) multiplexer_8 (
    .in0(pc_1), .in1(pc_1), .in2(beq_branch), .in3(blt_branch), .in4(pc_1), .in5(pc_1), .in6(pc_1),
    .in7(pc_1), .in8(pc_1), .in9(pc_1), .in10(pc_1), .in11(pc_1), .in12(j_addr), .in13(j_addr), .in14(pc_1),
    .in15(pc_1), .out(new_pc), .sel(opcode));
  RAM #(.addrWidth(16), .dataWidth(16), .trigger("high"), .databus("bibus")) ram_1 (
    .addr(memory_latch_1_address_latched), .we(memory_latch_1_we_latched), .oe(memory_latch_1_oe_latched),
    .din(memory_latch_1_data_in_latched), .dout(mem_out));
  assign bit_extender_7_out = {{10{imme[5]}}, imme};  // Bit_Extender bit_extender_7
  adder adder_5 (.a(pc_1), .b(bit_extender_7_out), .sub(1'b0), .out_4(adder_5_out_4));  // open: overflow
  Multiplexer #(.width(16), .enable("false")) multiplexer_9 (
    .in0(pc_1), .in1(adder_5_out_4), .out(blt_branch), .sel(and_3_out));
  and and_3 (and_3_out, Branch, blt);

  // Other names for the same wires on the sheet: L[5:0] = imme; shamt[2:0] = imme[2:0]; rd[2:0] = imme[5:3];
  //   rt[2:0] = L[8:6]; rs[2:0] = L[11:9]; write_mem = ALUsrc

  // Notes on the sheet:
  //   contents of rom_1 (hex, n*v repeats v):
  //   6100 6903 f008 62a0 e400 693f 313b 203f
endmodule

module memory_latch (
  input  [15:0] address,
  input  WE,
  input  clk,
  input  [15:0] data_in,
  output [15:0] address_latched,
  output WE_latched,
  output OE_latched,
  output [15:0] data_in_latched
);

  wire d_ff_1_q;
  wire [15:0] register_1_q;

  Register #(.width(16), .trigger("falling")) register_1 (
    .D(address), .en(WE), .clk(clk), .Q(register_1_q));  // open: clr
  D_Flip_Flop #(.trigger("falling")) d_ff_1 (.D(WE), .clk(clk), .Q(d_ff_1_q));  // open: Qn, preset, reset
  Register #(.width(16), .trigger("falling")) register_2 (
    .D(data_in), .en(WE), .clk(clk), .Q(data_in_latched));  // open: clr
  Multiplexer #(.width(16), .enable("false")) multiplexer_1 (
    .in0(address), .in1(register_1_q), .out(address_latched), .sel(d_ff_1_q));
  and and_1 (WE_latched, clk, d_ff_1_q);
  not not_1 (OE_latched, WE_latched);
endmodule

module RegisterFile (
  input  reset,
  input  [2:0] write_reg,
  input  [2:0] read_reg_1,
  input  [2:0] read_reg_2,
  input  [15:0] write_data,
  input  write_enable,
  input  clock,
  output [15:0] r1,
  output [15:0] r2
);

  wire decoder_1_out1, decoder_1_out2, decoder_1_out3, decoder_1_out4, decoder_1_out5, decoder_1_out6,
       decoder_1_out7, not_1_out;
  wire [15:0] singlereg_1_out_16bit, singlereg_2_out_16bit, singlereg_3_out_16bit, singlereg_4_out_16bit,
       singlereg_5_out_16bit, singlereg_6_out_16bit, singlereg_7_out_16bit;

  Decoder #(.select(3)) decoder_1 (
    .out1(decoder_1_out1), .out2(decoder_1_out2), .out3(decoder_1_out3), .out4(decoder_1_out4),
    .out5(decoder_1_out5), .out6(decoder_1_out6), .out7(decoder_1_out7), .sel(write_reg), .en(write_enable));  // open: out0
  not not_1 (not_1_out, clock);
  // Probe on {16{1'b0}}
  // Probe on nothing
  SingleReg singlereg_1 (
    .clock(not_1_out), .enable(decoder_1_out1), .in_16bit(write_data), .reset(reset),
    .out_16bit(singlereg_1_out_16bit));
  // Probe on singlereg_1_out_16bit
  // Probe on singlereg_2_out_16bit
  SingleReg singlereg_2 (
    .clock(not_1_out), .enable(decoder_1_out2), .in_16bit(write_data), .reset(reset),
    .out_16bit(singlereg_2_out_16bit));
  SingleReg singlereg_3 (
    .clock(not_1_out), .enable(decoder_1_out3), .in_16bit(write_data), .reset(reset),
    .out_16bit(singlereg_3_out_16bit));
  // Probe on singlereg_3_out_16bit
  SingleReg singlereg_4 (
    .clock(not_1_out), .enable(decoder_1_out4), .in_16bit(write_data), .reset(reset),
    .out_16bit(singlereg_4_out_16bit));
  // Probe on singlereg_4_out_16bit
  SingleReg singlereg_5 (
    .clock(not_1_out), .enable(decoder_1_out5), .in_16bit(write_data), .reset(reset),
    .out_16bit(singlereg_5_out_16bit));
  // Probe on singlereg_5_out_16bit
  SingleReg singlereg_6 (
    .clock(not_1_out), .enable(decoder_1_out6), .in_16bit(write_data), .reset(reset),
    .out_16bit(singlereg_6_out_16bit));
  // Probe on singlereg_6_out_16bit
  SingleReg singlereg_7 (
    .clock(not_1_out), .enable(decoder_1_out7), .in_16bit(write_data), .reset(reset),
    .out_16bit(singlereg_7_out_16bit));
  // Probe on singlereg_7_out_16bit
  Multiplexer #(.select(3), .width(16), .enable("false")) multiplexer_1 (
    .in0({16{1'b0}}), .in1(singlereg_1_out_16bit), .in2(singlereg_2_out_16bit), .in3(singlereg_3_out_16bit),
    .in4(singlereg_4_out_16bit), .in5(singlereg_5_out_16bit), .in6(singlereg_6_out_16bit),
    .in7(singlereg_7_out_16bit), .out(r1), .sel(read_reg_1));
  Multiplexer #(.select(3), .width(16), .enable("false")) multiplexer_2 (
    .in0({16{1'b0}}), .in1(singlereg_1_out_16bit), .in2(singlereg_2_out_16bit), .in3(singlereg_3_out_16bit),
    .in4(singlereg_4_out_16bit), .in5(singlereg_5_out_16bit), .in6(singlereg_6_out_16bit),
    .in7(singlereg_7_out_16bit), .out(r2), .sel(read_reg_2));
endmodule

module SingleReg (
  input  reset,
  input  clock,
  input  enable,
  input  [15:0] in_16bit,
  output [15:0] out_16bit
);

  wire and_1_out;

  and and_1 (and_1_out, clock, enable);
  D_Flip_Flop d_ff_1 (.D(in_16bit[0]), .clk(and_1_out), .Q(out_16bit[0]), .reset(reset));  // open: Qn, preset
  D_Flip_Flop d_ff_2 (.D(in_16bit[1]), .clk(and_1_out), .Q(out_16bit[1]), .reset(reset));  // open: Qn, preset
  D_Flip_Flop d_ff_3 (.D(in_16bit[2]), .clk(and_1_out), .Q(out_16bit[2]), .reset(reset));  // open: Qn, preset
  D_Flip_Flop d_ff_4 (.D(in_16bit[3]), .clk(and_1_out), .Q(out_16bit[3]), .reset(reset));  // open: Qn, preset
  D_Flip_Flop d_ff_5 (.D(in_16bit[4]), .clk(and_1_out), .Q(out_16bit[4]), .reset(reset));  // open: Qn, preset
  D_Flip_Flop d_ff_6 (.D(in_16bit[5]), .clk(and_1_out), .Q(out_16bit[5]), .reset(reset));  // open: Qn, preset
  D_Flip_Flop d_ff_7 (.D(in_16bit[6]), .clk(and_1_out), .Q(out_16bit[6]), .reset(reset));  // open: Qn, preset
  D_Flip_Flop d_ff_8 (.D(in_16bit[7]), .clk(and_1_out), .Q(out_16bit[7]), .reset(reset));  // open: Qn, preset
  D_Flip_Flop d_ff_9 (.D(in_16bit[8]), .clk(and_1_out), .Q(out_16bit[8]), .reset(reset));  // open: Qn, preset
  D_Flip_Flop d_ff_10 (.D(in_16bit[9]), .clk(and_1_out), .Q(out_16bit[9]), .reset(reset));  // open: Qn, preset
  D_Flip_Flop d_ff_11 (.D(in_16bit[10]), .clk(and_1_out), .Q(out_16bit[10]), .reset(reset));  // open: Qn, preset
  D_Flip_Flop d_ff_12 (.D(in_16bit[11]), .clk(and_1_out), .Q(out_16bit[11]), .reset(reset));  // open: Qn, preset
  D_Flip_Flop d_ff_13 (.D(in_16bit[12]), .clk(and_1_out), .Q(out_16bit[12]), .reset(reset));  // open: Qn, preset
  D_Flip_Flop d_ff_14 (.D(in_16bit[13]), .clk(and_1_out), .Q(out_16bit[13]), .reset(reset));  // open: Qn, preset
  D_Flip_Flop d_ff_15 (.D(in_16bit[14]), .clk(and_1_out), .Q(out_16bit[14]), .reset(reset));  // open: Qn, preset
  D_Flip_Flop d_ff_16 (.D(in_16bit[15]), .clk(and_1_out), .Q(out_16bit[15]), .reset(reset));  // open: Qn, preset
endmodule

module one_bit_full_adder (
  input  Cin,
  input  a,
  input  b,
  output Sum,
  output Cout
);

  wire and_1_out, and_2_out, xor_1_out;

  and and_1 (and_1_out, b, a);
  xor xor_1 (xor_1_out, a, b);
  or or_1 (Cout, and_1_out, and_2_out);
  and and_2 (and_2_out, xor_1_out, Cin);
  xor xor_2 (Sum, Cin, xor_1_out);
endmodule

module adder (
  input  sub,
  input  [15:0] a,
  input  [15:0] b,
  output [15:0] out_4,
  output overflow
);

  wire one_bit_full_adder_1_cout, one_bit_full_adder_2_cout, one_bit_full_adder_3_cout,
       one_bit_full_adder_4_cout, one_bit_full_adder_5_cout, one_bit_full_adder_6_cout,
       one_bit_full_adder_7_cout, one_bit_full_adder_8_cout, one_bit_full_adder_9_cout,
       one_bit_full_adder_10_cout, one_bit_full_adder_11_cout, one_bit_full_adder_12_cout,
       one_bit_full_adder_13_cout, one_bit_full_adder_14_cout, one_bit_full_adder_15_cout,
       one_bit_full_adder_16_cout, xor_1_out, xor_2_out, xor_3_out, xor_4_out, xor_5_out, xor_6_out,
       xor_7_out, xor_8_out, xor_9_out, xor_10_out, xor_11_out, xor_12_out, xor_13_out, xor_14_out,
       xor_15_out, xor_16_out;

  xor xor_1 (xor_1_out, b[0], sub);
  xor xor_2 (xor_2_out, b[1], sub);
  xor xor_3 (xor_3_out, b[2], sub);
  xor xor_4 (xor_4_out, b[3], sub);
  xor xor_5 (xor_5_out, b[4], sub);
  xor xor_6 (xor_6_out, b[5], sub);
  xor xor_7 (xor_7_out, b[6], sub);
  xor xor_8 (xor_8_out, b[7], sub);
  xor xor_9 (xor_9_out, b[8], sub);
  xor xor_10 (xor_10_out, b[9], sub);
  xor xor_11 (xor_11_out, b[10], sub);
  xor xor_12 (xor_12_out, b[11], sub);
  xor xor_13 (xor_13_out, b[12], sub);
  xor xor_14 (xor_14_out, b[13], sub);
  xor xor_15 (xor_15_out, b[14], sub);
  xor xor_16 (xor_16_out, b[15], sub);
  one_bit_full_adder one_bit_full_adder_1 (
    .Cin(sub), .a(a[0]), .b(xor_1_out), .Cout(one_bit_full_adder_1_cout), .Sum(out_4[0]));
  one_bit_full_adder one_bit_full_adder_2 (
    .Cin(one_bit_full_adder_1_cout), .a(a[1]), .b(xor_2_out), .Cout(one_bit_full_adder_2_cout), .Sum(out_4[1]));
  one_bit_full_adder one_bit_full_adder_3 (
    .Cin(one_bit_full_adder_2_cout), .a(a[2]), .b(xor_3_out), .Cout(one_bit_full_adder_3_cout), .Sum(out_4[2]));
  one_bit_full_adder one_bit_full_adder_4 (
    .Cin(one_bit_full_adder_3_cout), .a(a[3]), .b(xor_4_out), .Cout(one_bit_full_adder_4_cout), .Sum(out_4[3]));
  one_bit_full_adder one_bit_full_adder_5 (
    .Cin(one_bit_full_adder_4_cout), .a(a[4]), .b(xor_5_out), .Cout(one_bit_full_adder_5_cout), .Sum(out_4[4]));
  one_bit_full_adder one_bit_full_adder_6 (
    .Cin(one_bit_full_adder_5_cout), .a(a[5]), .b(xor_6_out), .Cout(one_bit_full_adder_6_cout), .Sum(out_4[5]));
  one_bit_full_adder one_bit_full_adder_7 (
    .Cin(one_bit_full_adder_6_cout), .a(a[6]), .b(xor_7_out), .Cout(one_bit_full_adder_7_cout), .Sum(out_4[6]));
  one_bit_full_adder one_bit_full_adder_8 (
    .Cin(one_bit_full_adder_7_cout), .a(a[7]), .b(xor_8_out), .Cout(one_bit_full_adder_8_cout), .Sum(out_4[7]));
  one_bit_full_adder one_bit_full_adder_9 (
    .Cin(one_bit_full_adder_8_cout), .a(a[8]), .b(xor_9_out), .Cout(one_bit_full_adder_9_cout), .Sum(out_4[8]));
  one_bit_full_adder one_bit_full_adder_10 (
    .Cin(one_bit_full_adder_9_cout), .a(a[9]), .b(xor_10_out), .Cout(one_bit_full_adder_10_cout),
    .Sum(out_4[9]));
  one_bit_full_adder one_bit_full_adder_11 (
    .Cin(one_bit_full_adder_10_cout), .a(a[10]), .b(xor_11_out), .Cout(one_bit_full_adder_11_cout),
    .Sum(out_4[10]));
  one_bit_full_adder one_bit_full_adder_12 (
    .Cin(one_bit_full_adder_11_cout), .a(a[11]), .b(xor_12_out), .Cout(one_bit_full_adder_12_cout),
    .Sum(out_4[11]));
  one_bit_full_adder one_bit_full_adder_13 (
    .Cin(one_bit_full_adder_12_cout), .a(a[12]), .b(xor_13_out), .Cout(one_bit_full_adder_13_cout),
    .Sum(out_4[12]));
  one_bit_full_adder one_bit_full_adder_14 (
    .Cin(one_bit_full_adder_13_cout), .a(a[13]), .b(xor_14_out), .Cout(one_bit_full_adder_14_cout),
    .Sum(out_4[13]));
  one_bit_full_adder one_bit_full_adder_15 (
    .Cin(one_bit_full_adder_14_cout), .a(a[14]), .b(xor_15_out), .Cout(one_bit_full_adder_15_cout),
    .Sum(out_4[14]));
  one_bit_full_adder one_bit_full_adder_16 (
    .Cin(one_bit_full_adder_15_cout), .a(a[15]), .b(xor_16_out), .Cout(one_bit_full_adder_16_cout),
    .Sum(out_4[15]));
  xor xor_17 (overflow, one_bit_full_adder_15_cout, one_bit_full_adder_16_cout);
endmodule

module ALU (
  input  [15:0] A,
  input  [15:0] B,
  input  [3:0] opcode,
  output [15:0] data_output
);

  wire [15:0] add, \and , left_shift, \or , right_shift, sub;

  adder adder_1 (.a(A), .b(B), .sub(1'b0), .out_4(add));  // open: overflow
  adder adder_2 (.a(A), .b(B), .sub(1'b1), .out_4(sub));  // open: overflow
  assign \or  = A | B;  // OR_Gate or_1, 16 bits wide
  assign \and  = A & B;  // AND_Gate and_1, 16 bits wide
  left_shifter left_shifter_1 (.data_input(A), .shift_number(B[3:0]), .out(left_shift));
  left_shifter left_shifter_2 (
    .data_input({A[0], A[1], A[2], A[3], A[4], A[5], A[6], A[7], A[8], A[9], A[10], A[11], A[12], A[13], A[14], A[15]}),
    .shift_number(B[3:0]),
    .out({right_shift[0], right_shift[1], right_shift[2], right_shift[3], right_shift[4], right_shift[5], right_shift[6], right_shift[7], right_shift[8], right_shift[9], right_shift[10], right_shift[11], right_shift[12], right_shift[13], right_shift[14], right_shift[15]}));
  Multiplexer #(.select(4), .width(16), .enable("false")) multiplexer_1 (
    .in0(add), .in1(add), .in4(\or ), .in5(\and ), .in6(add), .in7(add), .in8(sub), .in9(sub),
    .in10(right_shift), .in11(left_shift), .out(data_output), .sel(opcode));  // open: in2, in3, in12, in13, in14, in15

  // Other names for the same wires on the sheet: shift_number[3:0] = B[3:0]
endmodule

module left_shifter (
  input  [15:0] data_input,
  input  [3:0] shift_number,
  output [15:0] out
);

  wire multiplexer_1_out, multiplexer_2_out, multiplexer_3_out, multiplexer_4_out, multiplexer_5_out,
       multiplexer_6_out, multiplexer_7_out, multiplexer_8_out, multiplexer_9_out, multiplexer_10_out,
       multiplexer_11_out, multiplexer_12_out, multiplexer_13_out, multiplexer_14_out, multiplexer_15_out,
       multiplexer_16_out, multiplexer_17_out, multiplexer_18_out, multiplexer_19_out, multiplexer_20_out,
       multiplexer_21_out, multiplexer_22_out, multiplexer_23_out, multiplexer_24_out, multiplexer_25_out,
       multiplexer_26_out, multiplexer_27_out, multiplexer_28_out, multiplexer_29_out, multiplexer_30_out,
       multiplexer_31_out, multiplexer_32_out, multiplexer_33_out, multiplexer_34_out, multiplexer_35_out,
       multiplexer_36_out, multiplexer_37_out, multiplexer_38_out, multiplexer_39_out, multiplexer_40_out,
       multiplexer_41_out, multiplexer_42_out, multiplexer_43_out, multiplexer_44_out, multiplexer_45_out,
       multiplexer_46_out, multiplexer_47_out, multiplexer_48_out;

  Multiplexer #(.enable("false")) multiplexer_1 (
    .in0(data_input[15]), .in1(data_input[14]), .out(multiplexer_1_out), .sel(shift_number[0]));
  Multiplexer #(.enable("false")) multiplexer_2 (
    .in0(data_input[14]), .in1(data_input[13]), .out(multiplexer_2_out), .sel(shift_number[0]));
  Multiplexer #(.enable("false")) multiplexer_3 (
    .in0(data_input[13]), .in1(data_input[12]), .out(multiplexer_3_out), .sel(shift_number[0]));
  Multiplexer #(.enable("false")) multiplexer_4 (
    .in0(data_input[12]), .in1(data_input[11]), .out(multiplexer_4_out), .sel(shift_number[0]));
  Multiplexer #(.enable("false")) multiplexer_5 (
    .in0(data_input[11]), .in1(data_input[10]), .out(multiplexer_5_out), .sel(shift_number[0]));
  Multiplexer #(.enable("false")) multiplexer_6 (
    .in0(data_input[10]), .in1(data_input[9]), .out(multiplexer_6_out), .sel(shift_number[0]));
  Multiplexer #(.enable("false")) multiplexer_7 (
    .in0(data_input[9]), .in1(data_input[8]), .out(multiplexer_7_out), .sel(shift_number[0]));
  Multiplexer #(.enable("false")) multiplexer_8 (
    .in0(data_input[8]), .in1(data_input[7]), .out(multiplexer_8_out), .sel(shift_number[0]));
  Multiplexer #(.enable("false")) multiplexer_9 (
    .in0(data_input[7]), .in1(data_input[6]), .out(multiplexer_9_out), .sel(shift_number[0]));
  Multiplexer #(.enable("false")) multiplexer_10 (
    .in0(data_input[6]), .in1(data_input[5]), .out(multiplexer_10_out), .sel(shift_number[0]));
  Multiplexer #(.enable("false")) multiplexer_11 (
    .in0(data_input[5]), .in1(data_input[4]), .out(multiplexer_11_out), .sel(shift_number[0]));
  Multiplexer #(.enable("false")) multiplexer_12 (
    .in0(data_input[4]), .in1(data_input[3]), .out(multiplexer_12_out), .sel(shift_number[0]));
  Multiplexer #(.enable("false")) multiplexer_13 (
    .in0(data_input[3]), .in1(data_input[2]), .out(multiplexer_13_out), .sel(shift_number[0]));
  Multiplexer #(.enable("false")) multiplexer_14 (
    .in0(data_input[2]), .in1(data_input[1]), .out(multiplexer_14_out), .sel(shift_number[0]));
  Multiplexer #(.enable("false")) multiplexer_15 (
    .in0(data_input[1]), .in1(data_input[0]), .out(multiplexer_15_out), .sel(shift_number[0]));
  Multiplexer #(.enable("false")) multiplexer_16 (
    .in0(data_input[0]), .in1(1'b0), .out(multiplexer_16_out), .sel(shift_number[0]));
  Multiplexer #(.enable("false")) multiplexer_17 (
    .in0(multiplexer_1_out), .in1(multiplexer_3_out), .out(multiplexer_17_out), .sel(shift_number[1]));
  Multiplexer #(.enable("false")) multiplexer_18 (
    .in0(multiplexer_2_out), .in1(multiplexer_4_out), .out(multiplexer_18_out), .sel(shift_number[1]));
  Multiplexer #(.enable("false")) multiplexer_19 (
    .in0(multiplexer_3_out), .in1(multiplexer_5_out), .out(multiplexer_19_out), .sel(shift_number[1]));
  Multiplexer #(.enable("false")) multiplexer_20 (
    .in0(multiplexer_4_out), .in1(multiplexer_6_out), .out(multiplexer_20_out), .sel(shift_number[1]));
  Multiplexer #(.enable("false")) multiplexer_21 (
    .in0(multiplexer_5_out), .in1(multiplexer_7_out), .out(multiplexer_21_out), .sel(shift_number[1]));
  Multiplexer #(.enable("false")) multiplexer_22 (
    .in0(multiplexer_6_out), .in1(multiplexer_8_out), .out(multiplexer_22_out), .sel(shift_number[1]));
  Multiplexer #(.enable("false")) multiplexer_23 (
    .in0(multiplexer_7_out), .in1(multiplexer_9_out), .out(multiplexer_23_out), .sel(shift_number[1]));
  Multiplexer #(.enable("false")) multiplexer_24 (
    .in0(multiplexer_8_out), .in1(multiplexer_10_out), .out(multiplexer_24_out), .sel(shift_number[1]));
  Multiplexer #(.enable("false")) multiplexer_25 (
    .in0(multiplexer_9_out), .in1(multiplexer_11_out), .out(multiplexer_25_out), .sel(shift_number[1]));
  Multiplexer #(.enable("false")) multiplexer_26 (
    .in0(multiplexer_10_out), .in1(multiplexer_12_out), .out(multiplexer_26_out), .sel(shift_number[1]));
  Multiplexer #(.enable("false")) multiplexer_27 (
    .in0(multiplexer_11_out), .in1(multiplexer_13_out), .out(multiplexer_27_out), .sel(shift_number[1]));
  Multiplexer #(.enable("false")) multiplexer_28 (
    .in0(multiplexer_12_out), .in1(multiplexer_14_out), .out(multiplexer_28_out), .sel(shift_number[1]));
  Multiplexer #(.enable("false")) multiplexer_29 (
    .in0(multiplexer_13_out), .in1(multiplexer_15_out), .out(multiplexer_29_out), .sel(shift_number[1]));
  Multiplexer #(.enable("false")) multiplexer_30 (
    .in0(multiplexer_14_out), .in1(multiplexer_16_out), .out(multiplexer_30_out), .sel(shift_number[1]));
  Multiplexer #(.enable("false")) multiplexer_31 (
    .in0(multiplexer_15_out), .in1(1'b0), .out(multiplexer_31_out), .sel(shift_number[1]));
  Multiplexer #(.enable("false")) multiplexer_32 (
    .in0(multiplexer_16_out), .in1(1'b0), .out(multiplexer_32_out), .sel(shift_number[1]));
  Multiplexer #(.enable("false")) multiplexer_33 (
    .in0(multiplexer_17_out), .in1(multiplexer_21_out), .out(multiplexer_33_out), .sel(shift_number[2]));
  Multiplexer #(.enable("false")) multiplexer_34 (
    .in0(multiplexer_18_out), .in1(multiplexer_22_out), .out(multiplexer_34_out), .sel(shift_number[2]));
  Multiplexer #(.enable("false")) multiplexer_35 (
    .in0(multiplexer_19_out), .in1(multiplexer_23_out), .out(multiplexer_35_out), .sel(shift_number[2]));
  Multiplexer #(.enable("false")) multiplexer_36 (
    .in0(multiplexer_20_out), .in1(multiplexer_24_out), .out(multiplexer_36_out), .sel(shift_number[2]));
  Multiplexer #(.enable("false")) multiplexer_37 (
    .in0(multiplexer_21_out), .in1(multiplexer_25_out), .out(multiplexer_37_out), .sel(shift_number[2]));
  Multiplexer #(.enable("false")) multiplexer_38 (
    .in0(multiplexer_22_out), .in1(multiplexer_26_out), .out(multiplexer_38_out), .sel(shift_number[2]));
  Multiplexer #(.enable("false")) multiplexer_39 (
    .in0(multiplexer_23_out), .in1(multiplexer_27_out), .out(multiplexer_39_out), .sel(shift_number[2]));
  Multiplexer #(.enable("false")) multiplexer_40 (
    .in0(multiplexer_24_out), .in1(multiplexer_28_out), .out(multiplexer_40_out), .sel(shift_number[2]));
  Multiplexer #(.enable("false")) multiplexer_41 (
    .in0(multiplexer_25_out), .in1(multiplexer_29_out), .out(multiplexer_41_out), .sel(shift_number[2]));
  Multiplexer #(.enable("false")) multiplexer_42 (
    .in0(multiplexer_26_out), .in1(multiplexer_30_out), .out(multiplexer_42_out), .sel(shift_number[2]));
  Multiplexer #(.enable("false")) multiplexer_43 (
    .in0(multiplexer_27_out), .in1(multiplexer_31_out), .out(multiplexer_43_out), .sel(shift_number[2]));
  Multiplexer #(.enable("false")) multiplexer_44 (
    .in0(multiplexer_28_out), .in1(multiplexer_32_out), .out(multiplexer_44_out), .sel(shift_number[2]));
  Multiplexer #(.enable("false")) multiplexer_45 (
    .in0(multiplexer_29_out), .in1(1'b0), .out(multiplexer_45_out), .sel(shift_number[2]));
  Multiplexer #(.enable("false")) multiplexer_46 (
    .in0(multiplexer_30_out), .in1(1'b0), .out(multiplexer_46_out), .sel(shift_number[2]));
  Multiplexer #(.enable("false")) multiplexer_47 (
    .in0(multiplexer_31_out), .in1(1'b0), .out(multiplexer_47_out), .sel(shift_number[2]));
  Multiplexer #(.enable("false")) multiplexer_48 (
    .in0(multiplexer_32_out), .in1(1'b0), .out(multiplexer_48_out), .sel(shift_number[2]));
  Multiplexer #(.enable("false")) multiplexer_49 (
    .in0(multiplexer_33_out), .in1(multiplexer_41_out), .out(out[15]), .sel(shift_number[3]));
  Multiplexer #(.enable("false")) multiplexer_50 (
    .in0(multiplexer_34_out), .in1(multiplexer_42_out), .out(out[14]), .sel(shift_number[3]));
  Multiplexer #(.enable("false")) multiplexer_51 (
    .in0(multiplexer_35_out), .in1(multiplexer_43_out), .out(out[13]), .sel(shift_number[3]));
  Multiplexer #(.enable("false")) multiplexer_52 (
    .in0(multiplexer_36_out), .in1(multiplexer_44_out), .out(out[12]), .sel(shift_number[3]));
  Multiplexer #(.enable("false")) multiplexer_53 (
    .in0(multiplexer_37_out), .in1(multiplexer_45_out), .out(out[11]), .sel(shift_number[3]));
  Multiplexer #(.enable("false")) multiplexer_54 (
    .in0(multiplexer_38_out), .in1(multiplexer_46_out), .out(out[10]), .sel(shift_number[3]));
  Multiplexer #(.enable("false")) multiplexer_55 (
    .in0(multiplexer_39_out), .in1(multiplexer_47_out), .out(out[9]), .sel(shift_number[3]));
  Multiplexer #(.enable("false")) multiplexer_56 (
    .in0(multiplexer_40_out), .in1(multiplexer_48_out), .out(out[8]), .sel(shift_number[3]));
  Multiplexer #(.enable("false")) multiplexer_57 (
    .in0(multiplexer_41_out), .in1(1'b0), .out(out[7]), .sel(shift_number[3]));
  Multiplexer #(.enable("false")) multiplexer_58 (
    .in0(multiplexer_42_out), .in1(1'b0), .out(out[6]), .sel(shift_number[3]));
  Multiplexer #(.enable("false")) multiplexer_59 (
    .in0(multiplexer_43_out), .in1(1'b0), .out(out[5]), .sel(shift_number[3]));
  Multiplexer #(.enable("false")) multiplexer_60 (
    .in0(multiplexer_44_out), .in1(1'b0), .out(out[4]), .sel(shift_number[3]));
  Multiplexer #(.enable("false")) multiplexer_61 (
    .in0(multiplexer_45_out), .in1(1'b0), .out(out[3]), .sel(shift_number[3]));
  Multiplexer #(.enable("false")) multiplexer_62 (
    .in0(multiplexer_46_out), .in1(1'b0), .out(out[2]), .sel(shift_number[3]));
  Multiplexer #(.enable("false")) multiplexer_63 (
    .in0(multiplexer_47_out), .in1(1'b0), .out(out[1]), .sel(shift_number[3]));
  Multiplexer #(.enable("false")) multiplexer_64 (
    .in0(multiplexer_48_out), .in1(1'b0), .out(out[0]), .sel(shift_number[3]));

  // Other names for the same wires on the sheet: shift3 = shift_number[0]; shift2 = shift_number[1];
  //   shift1 = shift_number[2]; shift0 = shift_number[3]
endmodule
